# Fritzing sketch attiny (saved by Fritzing 1.0.1rc)
breadboards: 1

parts:
  U1 = attiny85 [package=dip]
  R2 = Photocell (LDR) [power=0.25W dark_resistance_@0.01lx=300kΩ light_resistance_@100lx=400Ω luminance=10lx package=THT]
  U2 = Arduino Uno (Rev3) - ICSP
  R1 = Resistor [tolerance=±5% power=0.25W resistance=10k package=THT]
  R3 = Resistor [tolerance=±5% power=0.25W resistance=10k package=THT]
  C1 = Electrolytic Capacitor [capacitance=10µF voltage=20V package="100 mil [THT, electrolytic]"]
  LED1 = smd LED [color="Red (633nm)" package="1206 [SMD]"]

nets:
  N1: U1.Pin_1, U2.D10_PWM/SS
  N2: U1.Pin_3, R2.pin_0, R3.Pin_1
  GND: U1.Pin_4, U2.GND, R3.Pin_0, C1.-
  N3: U1.Pin_5, U2.ICSP_MOSI, U2.D11_PWM/MOSI, R1.Pin_0
  N4: U1.Pin_6, U2.D12/MISO
  N5: U1.Pin_7, U2.D13/SCK
  5V: U1.Pin_8, R2.pin_1, U2.5V, LED1.cathode
  N6: U2.RESET, C1.+
  N7: R1.Pin_1, LED1.anode
