# Fritzing sketch esp32 (saved by Fritzing 1.0.1rc)
breadboards: 1

parts:
  M1 = ESP32-C3-DevKitM-1 [part_number=ESP32-C3-DevKitM-1]
  SSD1306 = SSD1306 0.96in 128x64 I2C Monochrome OLED Display
  R1 = Photocell (LDR) [power=0.25W dark_resistance_@0.01lx=300kΩ light_resistance_@100lx=400Ω luminance=10lx package=THT]
  R2 = Resistor [tolerance=±5% power=0.25W resistance=10k package=THT]

nets:
  GND: M1.GND-1, M1.GND-4, M1.GND-9, M1.GND-12, M1.GND-15, M1.GND-16, M1.GND-21, M1.GND-23, M1.GND-27, M1.GND-30, SSD1306.GND, R2.Pin_0
  3.3V: M1.3V3-17, M1.3V3-18, SSD1306.VCC, R1.pin_1
  N1: M1.2, SSD1306.SDA
  N2: M1.3, SSD1306.SCL
  N3: M1.0, R1.pin_0, R2.Pin_1
  N4: M1.5V-28, M1.5V-29

custom parts:
  ESP32-C3-DevKitM-1: Espressif Esp32 DevKit v1 is one of the development board created by DOIT to evaluate the ESP-WROOM-32 module. It is based on the ESP32 microcontroller that boasts Wifi, Bluetooth, Ethernet and Low Power support all in a single chip. (vanepp) Feb 2021: converted to ESP32-C3-DevKitM-1. This chip is 30pins long (2 x15) and 11 pins width.
